# Fritzing sketch esp plant monitor (saved by Fritzing 0.9.3b)

parts:
  Gizwits_WiFi_Witty_ESP-12F1 = Gizwits WiFi Witty ESP-12F
  Súčiastka1 = Analog Digital MUX Breakout
  C1 = Capacitor Polarized [package=panasonic_d]
  IC1 = Voltage Regulator [package=to-220-alt]
  Súčiastka2 = Soil Moisture Sensor
  S3 = Pushbutton [package="[SMD]"]
  S4 = Pushbutton [package="[SMD]"]
  U1 = LIPO-2000mAh [package=lipo-2000]
  R1 = Resistor [tolerance=±5% resistance=680k package="2010 [SMD]"]
  R2 = Resistor [tolerance=±5% resistance=148.7k package="2010 [SMD]"]
  Súčiastka3 = Soil Moisture Sensor
  Súčiastka4 = Soil Moisture Sensor
  Súčiastka5 = Soil Moisture Sensor
  Súčiastka6 = USB LiPoly Charger
  D1 = SOLAR-IXYS [package=solarbit-12x1]

nets:
  GND: Gizwits_WiFi_Witty_ESP-12F1.REST, Gizwits_WiFi_Witty_ESP-12F1.GPIO16, Gizwits_WiFi_Witty_ESP-12F1.GND, Gizwits_WiFi_Witty_ESP-12F1.GPIO0, Súčiastka1.GND, Súčiastka1.EN, IC1.GND, Súčiastka2.GND, S3.Pin_3, S3.Pin_4, S4.Pin_1, S4.Pin_2, U1.-, R2.Pin_1, Súčiastka3.GND, Súčiastka4.GND, Súčiastka5.GND, Súčiastka6.GND, D1.A
  N1: Gizwits_WiFi_Witty_ESP-12F1.ADC, R1.Pin_1, R2.Pin_0
  N2: Gizwits_WiFi_Witty_ESP-12F1.GPIO14, Súčiastka1.S2
  N3: Gizwits_WiFi_Witty_ESP-12F1.GPIO12, Súčiastka1.S0
  N4: Gizwits_WiFi_Witty_ESP-12F1.GPIO13, Súčiastka1.S1
  VCC: Gizwits_WiFi_Witty_ESP-12F1.VCC, Súčiastka1.C0, Súčiastka1.VCC, C1.+, U1.+, Súčiastka6.VBAT, D1.C
  N5: Gizwits_WiFi_Witty_ESP-12F1.GPIO4, Súčiastka1.S3
  N6: Gizwits_WiFi_Witty_ESP-12F1.GPIO5, IC1.IN
  N7: Súčiastka1.C1, Súčiastka2.SIG
  N8: Súčiastka1.C2, Súčiastka3.SIG
  N9: Súčiastka1.C3, Súčiastka4.SIG
  N10: Súčiastka1.C4, Súčiastka5.SIG
  N11: Súčiastka1.SIG, R1.Pin_0
  VCC_2: IC1.OUT, Súčiastka2.VCC, Súčiastka3.VCC, Súčiastka4.VCC, Súčiastka5.VCC
